// Logisim project cpu.circ as structural Verilog: 1 circuit, main circuit cpu
module cpu (
  input  clk,
  input  [31:0] Instruction,
  input  [31:0] MemReadData,
  output [31:0] MemAddress,
  output [31:0] ProgramCounter,
  output [31:0] ra,
  output [31:0] sp,
  output [31:0] t0,
  output [31:0] t1,
  output [31:0] t2,
  output [31:0] s0,
  output [31:0] s1,
  output [31:0] a0,
  output [3:0] MemWriteMask,
  output [31:0] MemWriteData
);

  wire imm7, imm20, memWEn;
  wire [2:0] funct3, immSel;
  wire [3:0] ALUSel, imm30_21;
  wire [4:1] imm11_7;
  wire [6:0] funct7, instr;
  wire [7:3] imm19_12;
  wire [31:0] A, adder_1_out, B, branch_store, I_imm_math, I_load, J_jal, J_jalr, R_format,
       regfile_1_regreaddata2, RegWriteData, S_format, U_auipc, U_lui, val1, val2, val3, val6, val7, val9,
       val10, val11, val14, val15, val16, val17, val18, val19, val20, val21, val22, val23, val26, val28,
       val29, val30, val31;

  Register #(.width(32)) PC (.D(adder_1_out), .clk(clk), .Q(ProgramCounter));  // open: en, clr
  Adder #(.width(32)) adder_1 (.a(ProgramCounter), .b(32'h4), .out(adder_1_out));  // open: cin, cout
  assign ALUSel = {{1{1'b0}}, funct3};  // Bit_Extender bit_extender_1
  control_logic control_logic_1 (
    .ImmSel(immSel), .ALUSel(ALUSel), .MemWEn(memWEn),
    .Instruction({funct7, imm30_21, imm20, imm19_12, funct3, imm11_7, imm7, instr}));  // open: PCSel, RegWEn, BrUn, ASel, BSel, WBSel, BrEq, BrLt
  regfile regfile_1 (
    .ReadReg1(imm19_12), .ReadReg2({imm30_21, imm20}), .WriteReg({imm11_7, imm7}),
    .RegWriteData(RegWriteData), .RegWEn(1'b1), .clk(clk), .ra(ra), .sp(sp), .t0(t0), .t1(t1), .t2(t2),
    .s0(s0), .s1(s1), .a0(a0), .RegReadData1(A), .RegReadData2(regfile_1_regreaddata2));
  imm_gen imm_gen_1 (
    .Instruction({funct7, imm30_21, imm20, imm19_12, funct3, imm11_7, imm7, instr}), .ImmSel(immSel),
    .Immediate(I_imm_math));
  Multiplexer #(.enable("false"), .select(5), .width(32)) multiplexer_1 (
    .in0(I_load), .in1(val1), .in2(val2), .in3(val3), .in4(I_imm_math), .in5(U_auipc), .in6(val6),
    .in7(val7), .in8(S_format), .in9(val9), .in10(val10), .in11(val11), .in12(R_format), .in13(U_lui),
    .in14(val14), .in15(val15), .in16(val16), .in17(val17), .in18(val18), .in19(val19), .in20(val20),
    .in21(val21), .in22(val22), .in23(val23), .in24(branch_store), .in25(J_jalr), .in26(val26), .in27(J_jal),
    .in28(val28), .in29(val29), .in30(val30), .in31(val31), .out(B), .sel(instr[6:2]));
  alu alu_1 (.ALUResult(RegWriteData), .A(A), .B(B), .ALUSel(ALUSel));
  // branch_comp branch_comp_1: pin names not known
  partial_store partial_store_1 (
    .Instruction({funct7, imm30_21, imm20, imm19_12, funct3, imm11_7, imm7, instr}), .MemAddress(MemAddress),
    .DataFromReg(RegWriteData), .MemWEn(memWEn), .MemWriteMask(MemWriteMask), .DataToMem(MemWriteData));
  partial_load partial_load_1 (
    .Instruction({funct7, imm30_21, imm20, imm19_12, funct3, imm11_7, imm7, instr}), .MemAddress(MemAddress));  // open: DataFromMem, DataToReg

  // Other names for the same wires on the sheet: imm19_12[2:0] = funct3;
  //   imm31_12[10:0] = {funct7, imm30_21[3:1], funct3[0]};
  //   instr[31:7] = {funct7, imm30_21, imm20, imm19_12, funct3, imm11_7, imm7};
  //   imm31_20[11:0] = {funct7, imm30_21, imm20}; rs2[4:0] = {imm30_21, imm20}; imm30_21[9:4] = funct7[5:0];
  //   imm30_25[5:0] = funct7[5:0]; imm31_25[6:0] = funct7; imm31 = funct7[6]; imm11_7[0] = imm7;
  //   rd[4:0] = {imm11_7, imm7}; imm11_8[3:0] = imm11_7; rs1[4:0] = imm19_12

  // Notes on the sheet:
  //   To IMEM
  //   IMEM (do **NOT** move this)
  //   From IMEM
  //   change later?
  //   change later?
  //   opcode
  //   funct3 (might have a problem being undefined)
  //   These determine what values go to A, B
  //   Inputs/Outputs for testing. Do **NOT** move these.
  //   It is OK to move the PC, RegFile, ALU, MEM, Branch Comp, Imm Gen, Partial Load, Partial Store and Control Logic to wherever is most convenient for you when constructing your CPU, and to delete this text
  //   always a register read value
  //   either a register read value or an immediate
  //   Opcodes:
  //   S-Format = 8
  //   R-Format: 12
  //   Branch / Store = 24
  //   J-Format --> jal: 27; jalr: 25
  //   U-Format --> lui = 13; auipc = 5
  //   I-Type --> immediate log/arith = 4; load = 0
  //   To DMEM
  //   DMEM (do **NOT** move this)
  //   From DMEM
endmodule
